# Fritzing sketch main (saved by Fritzing 0.9.3b)
breadboards: 1

parts:
  M1 = DC Motor
  M2 = DC Motor
  Part1 = Arduino Mega 2560 (Rev3)
  6V_Buck_Converter = RioRand LM2596
  V1 = DC Power [voltage=12V]
  IC1 = DIP - 8 pins [chip_label=Sabertooth-2x12-v2 package="DIP (Dual Inline) [THT]"]
  R1 = Resistor [tolerance=±5% resistance=10k package="2512 [SMD]"]

nets:
  N1: M1.pin_1, IC1.M2B
  N2: M1.pin_2, IC1.M2A
  N3: M2.pin_1, IC1.M1B
  N4: M2.pin_2, IC1.M1A
  N5: Part1.D18/TX1, IC1.S01, R1.Pin_0
  N6: Part1.VIN, 6V_Buck_Converter.Pin_3
  N7: Part1.GND, 6V_Buck_Converter.Pin_4
  N8: 6V_Buck_Converter.Pin_1, V1.V+, IC1.B+
  N9: 6V_Buck_Converter.Pin_2, V1.V-
  N10: IC1.0V, R1.Pin_1
  GND: IC1.B-

custom parts:
  DIP - 8 pins: A DIP stand-in part for whatever IC you want. With 8 pins on a 300mil dual inline package (DIP) footprint.
